# Fritzing sketch Schaltplan (saved by Fritzing 0.9.3b)
breadboards: 1

parts:
  Bauteil1 = Arduino Nano (Rev3.0)  # not connected
  RTC1 = DS3231 AT24C32 Real Time Clock  # not connected
  R1 = Resistor [tolerance=±5% resistance=1k package=THT]  # not connected
  DFRobot_DFPlayer_Mini1 = DFRobot DFPlayer Mini [part_number=DFR0299]
  X1 = USB Connectors [package=usb-a-pcb]  # not connected
  RGB_SMD_LED1 = SMD RGB LED (WS2812) [package=5050]  # not connected
  S1 = Round Pushbutton  # not connected
  S2 = SWITCH-MOMENTARY-2 [package=reed_switch_pth]  # not connected

nets:
  N1: DFRobot_DFPlayer_Mini1.GND-1, DFRobot_DFPlayer_Mini1.GND-2

custom parts:
  DS3231 AT24C32 Real Time Clock: Real-time clock basedo on chip DS3231, plus memory chip AT24C32 (32 Kb storage capacity). On-chip temperature sensor with an accuracy of ±3 ℃, I2C bus interface maximum speed: 400 kHz. Operating voltage: 3.3 V to 5.5 V with battery backup capabilities.
